// Logisim project TP1.circ as structural Verilog: 3 circuits, main circuit main
module main (
  output S1,
  output C1,
  output S2,
  output C2
);

  wire and_1_out, and_2_out, and_3_out, and_4_out, and_5_out, and_6_out, and_7_out, and_8_out, and_9_out,
       and_10_out, and_11_out, and_12_out, and_13_out, and_14_out, nor_1_out, nor_2_out, Switch_sw1,
       Switch_sw2, Switch_sw3, Switch_sw4, Switch_sw5;

  DipSwitch Switch (
    .sw1(Switch_sw1), .sw2(Switch_sw2), .sw3(Switch_sw3), .sw4(Switch_sw4), .sw5(Switch_sw5));  // open: sw6, sw7, sw8
  and and_1 (and_1_out, Switch_sw1, nor_2_out);
  and and_2 (and_2_out, Switch_sw2, nor_2_out);
  and and_3 (and_3_out, Switch_sw3, nor_2_out);
  and and_4 (and_4_out, Switch_sw1, Switch_sw2, Switch_sw3);
  and and_5 (and_5_out, Switch_sw1, Switch_sw2);
  and and_6 (and_6_out, Switch_sw1, Switch_sw3);
  and and_7 (and_7_out, Switch_sw2, Switch_sw3);
  and and_8 (and_8_out, nor_2_out, C2);
  and and_9 (and_9_out, Switch_sw5, C2);
  and and_10 (and_10_out, Switch_sw4, C2);
  and and_11 (and_11_out, nor_2_out, Switch_sw5, Switch_sw4);
  and and_12 (and_12_out, nor_2_out, Switch_sw5);
  and and_13 (and_13_out, nor_2_out, Switch_sw4);
  and and_14 (and_14_out, Switch_sw5, Switch_sw4);
  nor nor_1 (nor_1_out, and_1_out, and_2_out, and_3_out, and_4_out);
  nor nor_2 (nor_2_out, and_5_out, and_6_out, and_7_out);
  nor nor_3 (S2, and_8_out, and_9_out, and_10_out, and_11_out);
  nor nor_4 (C2, and_12_out, and_13_out, and_14_out);
  not not_1 (S1, nor_1_out);
  not not_2 (C1, nor_2_out);
endmodule

module Main2 (
  input  in_1,
  input  in_2,
  input  in_3,
  input  in_4,
  input  in_5,
  input  in_6,
  input  in_7,
  output ZG,
  output ZP,
  output ZE
);

  wire and_1_out, and_2_out, and_3_out, and_4_out, and_5_out, and_6_out, and_7_out, and_8_out, and_9_out,
       and_10_out, not_1_out, not_2_out, not_3_out, not_4_out, not_5_out, not_6_out, or_1_out, or_2_out;

  not not_1 (not_1_out, in_1);
  not not_2 (not_2_out, in_2);
  not not_3 (not_3_out, in_3);
  not not_4 (not_4_out, in_4);
  and and_1 (and_1_out, not_1_out, in_2);
  and and_2 (and_2_out, in_1, not_2_out);
  and and_3 (and_3_out, not_3_out, in_4);
  and and_4 (and_4_out, in_3, not_4_out);
  or or_1 (or_1_out, and_1_out, and_2_out);
  or or_2 (or_2_out, and_3_out, and_4_out);
  not not_5 (not_5_out, or_1_out);
  not not_6 (not_6_out, or_2_out);
  and and_5 (and_5_out, in_2, not_1_out);
  and and_6 (and_6_out, not_2_out, in_1);
  and and_7 (and_7_out, in_4, not_5_out, not_3_out);
  and and_8 (and_8_out, not_4_out, not_5_out, in_3);
  and and_9 (and_9_out, not_5_out, not_6_out, in_5);
  and and_10 (and_10_out, not_5_out, not_6_out, in_6);
  and and_11 (ZE, not_5_out, not_6_out, in_7);
  or or_3 (ZG, and_6_out, and_8_out, and_9_out);
  or or_4 (ZP, and_5_out, and_7_out, and_10_out);
endmodule

module Nand1 (
  output out_1,
  output out_2,
  output out_3,
  output out_4
);

  wire and_1_out, and_2_out, and_3_out, and_4_out, and_5_out, and_6_out, and_7_out, dipswitch_1_sw1,
       dipswitch_1_sw2, dipswitch_1_sw3, dipswitch_1_sw4, dipswitch_1_sw5, nand_1_out, nand_2_out,
       nand_3_out, nand_4_out, nand_5_out, nand_6_out, nand_7_out, nand_8_out, nand_9_out, nand_10_out,
       nand_11_out, nand_12_out, nand_13_out, nand_14_out, nand_15_out, nand_16_out, nand_17_out;

  DipSwitch dipswitch_1 (
    .sw1(dipswitch_1_sw1), .sw2(dipswitch_1_sw2), .sw3(dipswitch_1_sw3), .sw4(dipswitch_1_sw4),
    .sw5(dipswitch_1_sw5));  // open: sw6, sw7, sw8
  nand nand_1 (nand_1_out, dipswitch_1_sw1, out_2);
  nand nand_2 (nand_2_out, dipswitch_1_sw2, out_2);
  nand nand_3 (nand_3_out, dipswitch_1_sw3, out_2);
  nand nand_4 (nand_4_out, dipswitch_1_sw1, dipswitch_1_sw2, dipswitch_1_sw3);
  nand nand_5 (nand_5_out, dipswitch_1_sw1, dipswitch_1_sw2);
  nand nand_6 (nand_6_out, dipswitch_1_sw1, dipswitch_1_sw3);
  nand nand_7 (nand_7_out, dipswitch_1_sw2, dipswitch_1_sw3);
  and and_1 (and_1_out, out_2, out_4);
  and and_2 (and_2_out, dipswitch_1_sw5, out_4);
  and and_3 (and_3_out, dipswitch_1_sw4, out_4);
  and and_4 (and_4_out, out_2, dipswitch_1_sw5, dipswitch_1_sw4);
  and and_5 (and_5_out, out_2, dipswitch_1_sw5);
  and and_6 (and_6_out, out_2, dipswitch_1_sw4);
  and and_7 (and_7_out, dipswitch_1_sw5, dipswitch_1_sw4);
  nand nand_8 (nand_8_out, nand_1_out, nand_1_out);
  nand nand_9 (nand_9_out, nand_2_out, nand_2_out);
  nand nand_10 (nand_10_out, nand_3_out, nand_3_out);
  nand nand_11 (nand_11_out, nand_4_out, nand_4_out);
  nand nand_12 (nand_12_out, nand_5_out, nand_5_out);
  nand nand_13 (nand_13_out, nand_6_out, nand_6_out);
  nand nand_14 (nand_14_out, nand_7_out, nand_7_out);
  nor nor_1 (out_3, and_1_out, and_2_out, and_3_out, and_4_out);
  nor nor_2 (out_4, and_5_out, and_6_out, and_7_out);
  nand nand_15 (nand_15_out, nand_8_out, nand_9_out);
  nand nand_16 (nand_16_out, nand_10_out, nand_11_out);
  nand nand_17 (nand_17_out, nand_12_out, nand_13_out, nand_14_out);
  nand nand_18 (out_1, nand_15_out, nand_16_out);
  nand nand_19 (out_2, nand_17_out, nand_17_out);
endmodule
