// Logisim project TP2.circ as structural Verilog: 9 circuits, main circuit main
module main (
  input  in_1,
  input  in_2,
  input  in_3,
  input  in_4
);

  wire decodeur_1_a, decodeur_1_b, decodeur_1_c, decodeur_1_d, decodeur_1_e, decodeur_1_f, decodeur_1_g;

  decodeur decodeur_1 (
    .W(in_1), .X(in_2), .Y(in_3), .Z(in_4), .a(decodeur_1_a), .b(decodeur_1_b), .c(decodeur_1_c),
    .d(decodeur_1_d), .e(decodeur_1_e), .f(decodeur_1_f), .g(decodeur_1_g));
  _7_Segment_Display u_7_segment_display_1 (
    .g(decodeur_1_g), .f(decodeur_1_f), .a(decodeur_1_a), .b(decodeur_1_b), .e(decodeur_1_e),
    .d(decodeur_1_d), .c(decodeur_1_c));  // open: dp
endmodule

module a1 (
  input  W,
  input  X,
  input  Y,
  input  Z,
  output o
);

  wire not_1_out, not_2_out, not_3_out, not_4_out, not_5_out, WXY_out, WXZ_out, WY_out, WZ_out, XY_out,
       XZ_out;

  not not_1 (not_1_out, W);
  not not_2 (not_2_out, X);
  not not_3 (not_3_out, Z);
  not not_4 (not_4_out, X);
  not not_5 (not_5_out, Y);
  and WZ (WZ_out, W, not_3_out);
  and WY (WY_out, not_1_out, Y);
  and XY (XY_out, X, Y);
  and XZ (XZ_out, not_2_out, not_3_out);
  and WXY (WXY_out, W, not_4_out, not_5_out);
  and WXZ (WXZ_out, not_1_out, X, Z);
  or or_1 (o, WZ_out, WY_out, XY_out, XZ_out, WXY_out, WXZ_out);
endmodule

module b1 (
  input  W,
  input  X,
  input  Y,
  input  Z,
  output o
);

  wire not_1_out, not_2_out, not_3_out, not_4_out, WX_out, WYZ2_out, WYZ3_out, WYZ_out, XY_out, XZ_out;

  not not_1 (not_1_out, W);
  not not_2 (not_2_out, X);
  not not_3 (not_3_out, Y);
  not not_4 (not_4_out, Z);
  and WX (WX_out, not_1_out, not_2_out);
  and WYZ (WYZ_out, not_1_out, not_3_out, not_4_out);
  and XY (XY_out, not_2_out, not_3_out);
  and XZ (XZ_out, not_2_out, not_4_out);
  and WYZ2 (WYZ2_out, not_1_out, Y, Z);
  and WYZ3 (WYZ3_out, W, not_3_out, Z);
  or or_1 (o, WX_out, WYZ_out, XY_out, XZ_out, WYZ2_out, WYZ3_out);
endmodule

module c1 (
  input  W,
  input  X,
  input  Y,
  input  Z,
  output C
);

  wire not_1_out, not_2_out, not_3_out, WX2_out, WX_out, WY_out, WZ_out, YZ_out;

  not not_1 (not_1_out, W);
  not not_2 (not_2_out, Y);
  not not_3 (not_3_out, X);
  and WY (WY_out, not_1_out, not_2_out);
  and WZ (WZ_out, not_1_out, Z);
  and YZ (YZ_out, not_2_out, Z);
  and WX (WX_out, not_1_out, X);
  and WX2 (WX2_out, W, not_3_out);
  or or_1 (C, WY_out, WZ_out, YZ_out, WX_out, WX2_out);
endmodule

module decodeur (
  input  W,
  input  X,
  input  Y,
  input  Z,
  output a,
  output b,
  output c,
  output d,
  output e,
  output f,
  output g
);

  a1 a1_1 (.W(W), .X(X), .Y(Y), .Z(Z), .o(a));
  b1 b1_1 (.W(W), .X(X), .Y(Y), .Z(Z), .o(b));
  c1 c1_1 (.W(W), .X(X), .Y(Y), .Z(Z), .C(c));
  d1 d1_1 (.W(W), .X(X), .Y(Y), .Z(Z), .O(d));
  e1 e1_1 (.W(W), .X(X), .Y(Y), .Z(Z), .O(e));
  f1 f1_1 (.W(W), .X(X), .Y(Y), .Z(Z), .O(f));
  g1 g1_1 (.W(W), .X(X), .Y(Y), .Z(Z), .O(g));
endmodule

module d1 (
  input  W,
  input  X,
  input  Y,
  input  Z,
  output O
);

  wire not_1_out, not_2_out, not_3_out, not_4_out, WXZ_out, WY_out, XYZ2_out, XYZ3_out, XYZ_out;

  not not_1 (not_1_out, W);
  not not_2 (not_2_out, X);
  not not_3 (not_3_out, Z);
  not not_4 (not_4_out, Y);
  and WXZ (WXZ_out, not_1_out, not_2_out, not_3_out);
  and XYZ (XYZ_out, not_2_out, Y, Z);
  and XYZ2 (XYZ2_out, X, not_4_out, Z);
  and XYZ3 (XYZ3_out, X, Y, not_3_out);
  and WY (WY_out, W, not_4_out);
  or or_1 (O, WXZ_out, XYZ_out, XYZ2_out, XYZ3_out, WY_out);
endmodule

module e1 (
  input  W,
  input  X,
  input  Y,
  input  Z,
  output O
);

  wire not_1_out, not_2_out, WX_out, WY_out, XZ_out, YZ_out;

  not not_1 (not_1_out, Z);
  not not_2 (not_2_out, X);
  and XZ (XZ_out, not_2_out, not_1_out);
  and YZ (YZ_out, Y, not_1_out);
  and WY (WY_out, W, Y);
  and WX (WX_out, W, X);
  or or_1 (O, XZ_out, YZ_out, WY_out, WX_out);
endmodule

module f1 (
  input  W,
  input  X,
  input  Y,
  input  Z,
  output O
);

  wire not_1_out, not_2_out, not_3_out, not_4_out, not_5_out, WX_out, WXY_out, WY_out, XZ_out, YZ_out;

  not not_1 (not_1_out, Y);
  not not_2 (not_2_out, Z);
  not not_3 (not_3_out, W);
  not not_4 (not_4_out, Y);
  not not_5 (not_5_out, X);
  and YZ (YZ_out, not_1_out, not_2_out);
  and WXY (WXY_out, not_3_out, X, not_4_out);
  and XZ (XZ_out, X, not_2_out);
  and WX (WX_out, W, not_5_out);
  and WY (WY_out, W, Y);
  or or_1 (O, YZ_out, WXY_out, XZ_out, WX_out, WY_out);
endmodule

module g1 (
  input  W,
  input  X,
  input  Y,
  input  Z,
  output O
);

  wire not_1_out, not_2_out, not_3_out, not_4_out, WX_out, WXY_out, WZ_out, XY_out, YZ_out;

  not not_1 (not_1_out, X);
  not not_2 (not_2_out, Z);
  not not_3 (not_3_out, W);
  not not_4 (not_4_out, Y);
  and XY (XY_out, not_1_out, Y);
  and YZ (YZ_out, Y, not_2_out);
  and WXY (WXY_out, not_3_out, X, not_4_out);
  and WX (WX_out, W, not_1_out);
  and WZ (WZ_out, W, Z);
  or or_1 (O, XY_out, YZ_out, WXY_out, WX_out, WZ_out);
endmodule
