// Logisim project TP3_2.circ as structural Verilog: 2 circuits, main circuit main
module main (
  input  reset,
  input  Control,
  output out_3,
  output out_4,
  output out_5
);

  wire and_1_out, and_2_out, and_3_out, and_4_out, and_5_out, and_6_out, and_7_out, buffer_1_out,
       buffer_2_out, not_1_out, not_2_out, or_1_out, or_2_out, or_3_out, sr_1_o_, sr_3_o_;

  and and_1 (and_1_out, out_5, out_4);
  buf buffer_1 (buffer_1_out, reset);
  buf buffer_2 (buffer_2_out, reset);
  and and_2 (and_2_out, Control, sr_3_o_);
  not not_1 (not_1_out, Control);
  and and_3 (and_3_out, not_1_out, and_1_out);
  and and_4 (and_4_out, ~out_4, ~out_3, ~Control);  // AND_Gate
  or or_1 (or_1_out, reset, and_3_out);
  or or_2 (or_2_out, and_6_out, buffer_1_out);
  or or_3 (or_3_out, and_4_out, buffer_2_out);
  sr sr_1 (.R(or_1_out), .S(and_2_out), .O(out_3), .O_(sr_1_o_));
  not not_2 (not_2_out, Control);
  sr sr_2 (.R(or_2_out), .S(and_5_out), .O(out_4));  // open: O_
  sr sr_3 (.R(or_3_out), .S(and_7_out), .O(out_5), .O_(sr_3_o_));
  and and_5 (and_5_out, out_3, not_2_out);
  and and_6 (and_6_out, sr_1_o_, Control, out_5);
  and and_7 (and_7_out, out_4, Control);
endmodule

module sr (
  input  R,
  input  S,
  output O,
  output O_
);

  nor nor_1 (O, R, O_);
  nor nor_2 (O_, O, S);
endmodule
