// Logisim project tp3.circ as structural Verilog: 5 circuits, main circuit main
module main (
  input  one_one,
  input  one_two,
  input  one_three,
  input  one_four,
  input  two_one,
  input  two_two,
  input  two_three,
  input  two_four,
  output overflow,
  output out_10,
  output out_11,
  output out_12,
  output out_13,
  output out_14,
  output out_15,
  output out_16,
  output out_17,
  output under,
  output underflow
);

  additionneur additionneur_1 (
    .a1(one_one), .a2(two_one), .b1(one_two), .b2(two_two), .c1(one_three), .c2(two_three), .d1(one_four),
    .d2(two_four), .out_a(out_10), .out_b(out_11), .out_c(out_12), .out_d(out_13), .overflow(overflow));
  Substractor substractor_1 (
    .a1(one_one), .a2(two_one), .b1(one_two), .b2(two_two), .c1(one_three), .c2(two_three), .d1(one_four),
    .d2(two_four), .out_1(out_14), .out_2(out_15), .out_3(out_16), .out_4(out_17), .underflow(under));
endmodule

module additionneur (
  input  a1,
  input  a2,
  input  b1,
  input  b2,
  input  c1,
  input  c2,
  input  d1,
  input  d2,
  output out_a,
  output out_b,
  output out_c,
  output out_d,
  output overflow
);

  wire add_1_c_out, add_2_c_out, and_1_out;

  xor xor_1 (out_a, a1, a2);
  and and_1 (and_1_out, a1, a2);
  add add_1 (.c_in(and_1_out), .a(b1), .b(b2), .S(out_b), .c_out(add_1_c_out));
  add add_2 (.c_in(add_1_c_out), .a(c1), .b(c2), .S(out_c), .c_out(add_2_c_out));
  add add_3 (.c_in(add_2_c_out), .a(d1), .b(d2), .S(out_d), .c_out(overflow));
endmodule

module add (
  input  c_in,
  input  a,
  input  b,
  output S,
  output c_out
);

  wire and_1_out, and_2_out, xor_1_out;

  xor xor_1 (xor_1_out, a, b);
  xor xor_2 (S, c_in, xor_1_out);
  and and_1 (and_1_out, a, b);
  and and_2 (and_2_out, c_in, xor_1_out);
  or or_1 (c_out, and_1_out, and_2_out);
endmodule

module Substractor (
  input  a1,
  input  a2,
  input  b1,
  input  b2,
  input  c1,
  input  c2,
  input  d1,
  input  d2,
  output out_1,
  output out_2,
  output out_3,
  output out_4,
  output underflow
);

  wire CAR_out, not_1_out, sub_1_c_out, sub_2_c_out;

  not not_1 (not_1_out, a1);
  xor xor_1 (out_1, a1, a2);
  and CAR (CAR_out, not_1_out, a2);
  sub sub_1 (.a(b1), .b(b2), .c_in(CAR_out), .s_out(out_2), .c_out(sub_1_c_out));
  sub sub_2 (.a(c1), .b(c2), .c_in(sub_1_c_out), .s_out(out_3), .c_out(sub_2_c_out));
  sub sub_3 (.a(d1), .b(d2), .c_in(sub_2_c_out), .s_out(out_4), .c_out(underflow));
endmodule

module sub (
  input  a,
  input  b,
  input  c_in,
  output s_out,
  output c_out
);

  wire and_1_out, and_2_out, not_1_out, not_2_out, xor_1_out;

  not not_1 (not_1_out, a);
  xor xor_1 (xor_1_out, a, b);
  and and_1 (and_1_out, not_1_out, b);
  not not_2 (not_2_out, xor_1_out);
  and and_2 (and_2_out, not_2_out, c_in);
  or or_1 (c_out, and_2_out, and_1_out);
  xor xor_2 (s_out, xor_1_out, c_in);
endmodule
