// Logisim project tp4.circ as structural Verilog
module main (
);

  wire button_1_out, clock_1_out, convertisseur_1_bot, convertisseur_1_center, convertisseur_1_l_h,
       convertisseur_1_l_l, convertisseur_1_r_h, convertisseur_1_r_l, convertisseur_1_top,
       convertisseur_2_bot, convertisseur_2_center, convertisseur_2_l_h, convertisseur_2_l_l,
       convertisseur_2_r_h, convertisseur_2_r_l, convertisseur_2_top, convertisseur_3_bot,
       convertisseur_3_center, convertisseur_3_l_h, convertisseur_3_l_l, convertisseur_3_r_h,
       convertisseur_3_r_l, convertisseur_3_top, lcs_1_c_out, lcs_1_high, lcs_1_low, lcs_2_c_out, lcs_2_high,
       lcs_2_low, lcs_3_high, lcs_3_low;

  Clock clock_1 (.out(clock_1_out));
  Button button_1 (.out(button_1_out));
  LCS lcs_1 (
    .Clock(clock_1_out), .C_IN(1'b1), .Reset(button_1_out), .C_OUT(lcs_1_c_out), .Low(lcs_1_low),
    .High(lcs_1_high));
  LCS lcs_2 (
    .Clock(clock_1_out), .C_IN(lcs_1_c_out), .Reset(button_1_out), .C_OUT(lcs_2_c_out), .Low(lcs_2_low),
    .High(lcs_2_high));
  LCS lcs_3 (
    .Clock(clock_1_out), .C_IN(lcs_2_c_out), .Reset(button_1_out), .Low(lcs_3_low), .High(lcs_3_high));  // open: C_OUT
  Convertisseur convertisseur_1 (
    .Low(lcs_1_low), .High(lcs_1_high), .center(convertisseur_1_center), .L_H(convertisseur_1_l_h),
    .top(convertisseur_1_top), .R_H(convertisseur_1_r_h), .R_L(convertisseur_1_r_l),
    .BOT(convertisseur_1_bot), .L_L(convertisseur_1_l_l));
  Convertisseur convertisseur_2 (
    .Low(lcs_2_low), .High(lcs_2_high), .center(convertisseur_2_center), .L_H(convertisseur_2_l_h),
    .top(convertisseur_2_top), .R_H(convertisseur_2_r_h), .R_L(convertisseur_2_r_l),
    .BOT(convertisseur_2_bot), .L_L(convertisseur_2_l_l));
  Convertisseur convertisseur_3 (
    .Low(lcs_3_low), .High(lcs_3_high), .center(convertisseur_3_center), .L_H(convertisseur_3_l_h),
    .top(convertisseur_3_top), .R_H(convertisseur_3_r_h), .R_L(convertisseur_3_r_l),
    .BOT(convertisseur_3_bot), .L_L(convertisseur_3_l_l));
  _7_Segment_Display u_7_segment_display_1 (
    .g(convertisseur_1_center), .f(convertisseur_1_l_h), .a(convertisseur_1_top), .b(convertisseur_1_r_h),
    .e(convertisseur_1_l_l), .d(convertisseur_1_bot), .c(convertisseur_1_r_l), .dp(1'b0));
  _7_Segment_Display u_7_segment_display_2 (
    .g(convertisseur_2_center), .f(convertisseur_2_l_h), .a(convertisseur_2_top), .b(convertisseur_2_r_h),
    .e(convertisseur_2_l_l), .d(convertisseur_2_bot), .c(convertisseur_2_r_l), .dp(1'b0));
  _7_Segment_Display u_7_segment_display_3 (
    .g(convertisseur_3_center), .f(convertisseur_3_l_h), .a(convertisseur_3_top), .b(convertisseur_3_r_h),
    .e(convertisseur_3_l_l), .d(convertisseur_3_bot), .c(convertisseur_3_r_l), .dp(1'b0));
endmodule

module LBS (
  input  Clock,
  input  C_in,
  input  Reset,
  output C_out,
  output one,
  output two,
  output three
);

  wire and_1_out, nand_1_out, or_1_out;

  and and_1 (and_1_out, Clock, C_in);
  nand nand_1 (nand_1_out, or_1_out, Clock);
  or or_1 (or_1_out, three, two, one);
  D_Flip_Flop d_ff_1 (.D(nand_1_out), .clk(and_1_out), .Q(one), .reset(Reset));  // open: Qn, preset
  D_Flip_Flop d_ff_2 (.D(one), .clk(and_1_out), .Q(two), .reset(Reset));  // open: Qn, preset
  D_Flip_Flop d_ff_3 (.D(two), .clk(and_1_out), .Q(three), .reset(Reset));  // open: Qn, preset
  and and_2 (C_out, C_in, three);
endmodule

module LCS (
  input  Clock,
  input  C_IN,
  input  Reset,
  output C_OUT,
  output Low,
  output High
);

  wire and_1_out, and_2_out, d_ff_1_q, d_ff_2_q, d_ff_3_q, nand_1_out, nand_2_out, or_1_out;

  and and_1 (and_1_out, Clock, C_IN);
  nand nand_1 (nand_1_out, or_1_out, Clock);
  or or_1 (or_1_out, d_ff_2_q, d_ff_1_q);
  D_Flip_Flop d_ff_1 (.D(nand_1_out), .clk(and_1_out), .Q(d_ff_1_q), .reset(Reset));  // open: Qn, preset
  D_Flip_Flop d_ff_2 (.D(d_ff_1_q), .clk(and_1_out), .Q(d_ff_2_q), .reset(Reset));  // open: Qn, preset
  nand nand_2 (nand_2_out, d_ff_3_q, Clock);
  and and_2 (and_2_out, d_ff_2_q, Clock);
  D_Flip_Flop #(.trigger("falling")) d_ff_3 (
    .D(nand_2_out), .clk(and_2_out), .Q(d_ff_3_q), .reset(Reset));  // open: Qn, preset
  Ternary ternary_1 (.a(d_ff_1_q), .b(d_ff_2_q), .Low(Low), .High(High));
  and and_3 (C_OUT, C_IN, d_ff_3_q);
endmodule

module Convertisseur (
  input  Low,
  input  High,
  output center,
  output L_H,
  output top,
  output R_H,
  output R_L,
  output BOT,
  output L_L
);

  wire and_3_out, and_4_out, and_5_out, and_6_out, and_7_out, and_8_out, not_1_out, not_2_out, not_3_out,
       not_4_out, not_5_out, not_6_out, not_7_out, not_8_out;

  not not_1 (not_1_out, Low);
  not not_2 (not_2_out, High);
  and and_1 (L_H, Low, High);
  not not_3 (not_3_out, Low);
  not not_4 (not_4_out, High);
  or or_1 (R_L, High, Low);
  not not_5 (not_5_out, Low);
  not not_6 (not_6_out, High);
  not not_7 (not_7_out, Low);
  not not_8 (not_8_out, High);
  and and_2 (center, not_1_out, not_2_out);
  and and_3 (and_3_out, not_3_out, not_4_out);
  and and_4 (and_4_out, Low, High);
  and and_5 (and_5_out, not_5_out, not_6_out);
  and and_6 (and_6_out, Low, High);
  and and_7 (and_7_out, not_7_out, not_8_out);
  and and_8 (and_8_out, Low, High);
  or or_2 (top, and_3_out, and_4_out);
  or or_3 (BOT, and_5_out, and_6_out);
  or or_4 (L_L, and_7_out, and_8_out);

  assign R_H = 1'b1;
endmodule

module Ternary (
  input  a,
  input  b,
  output Low,
  output High
);

  wire not_1_out, not_2_out;

  not not_1 (not_1_out, a);
  not not_2 (not_2_out, b);
  not not_3 (High, b);
  and and_1 (Low, not_1_out, not_2_out);
endmodule
